// Logisim project progetto.circ as structural Verilog: 1 circuit, main circuit main
module main (
);

  wire _0_out, _1_out, _2_out, _3_out, _4_out, _5_out, _6_out, _7_out, _8_out, _9_out, annulla_out,
       azzera_out, button_2_out, button_out, clock_1_out, m_calcolatore_1_of, m_selection_displayer_1_out_2,
       m_selection_displayer_1_out_3, m_selection_displayer_1_out_4, m_ui_1_p17, m_ui_1_p19, m_ui_1_p21,
       m_ui_1_p23, m_ui_1_p24, m_ui_1_p25, m_ui_1_p26, m_ui_1_p27, m_ui_1_p28, m_ui_1_p29, m_ui_1_p30,
       m_ui_1_p31, ok_out, reset_out;
  wire [1:0] op_code, select;
  wire [2:0] m_op_code_displayer_1_out_2, m_op_code_displayer_1_out_3, m_op_code_displayer_1_out_4;
  wire [3:0] m_input_memory_1_q, m_input_memory_1_q_saved, m_input_memory_1_x, m_input_memory_1_x_2,
       m_input_memory_1_x_2_saved, m_input_memory_1_x_saved, m_ui_1_p22;
  wire [4:0] m_calcolatore_1_x, m_calcolatore_1_y;
  wire [31:0] m_drawer_1_p8, m_drawer_1_p9, m_drawer_1_p10, m_drawer_1_p11, m_drawer_1_p12, m_drawer_1_p13,
       m_drawer_1_p14, m_drawer_1_p15, m_drawer_1_p16, m_drawer_1_p17, m_drawer_1_p18, m_drawer_1_p19,
       m_drawer_1_p20, m_drawer_1_p21, m_drawer_1_p22, m_drawer_1_p23, m_drawer_1_p24, m_drawer_1_p25,
       m_drawer_1_p26, m_drawer_1_p27, m_drawer_1_p28, m_drawer_1_p29, m_drawer_1_p30, m_drawer_1_p31,
       m_drawer_1_p32, m_drawer_1_p33, m_drawer_1_p34, m_drawer_1_p35, m_drawer_1_p36, m_drawer_1_p37,
       m_drawer_1_p38, m_drawer_1_p39;

  Button _7 (.out(_7_out));
  Button _4 (.out(_4_out));
  Button _1 (.out(_1_out));
  Button ok (.out(ok_out));
  Button reset (.out(reset_out));
  Button _9 (.out(_9_out));
  Button _8 (.out(_8_out));
  Button _5 (.out(_5_out));
  Button _6 (.out(_6_out));
  Button _2 (.out(_2_out));
  Button _3 (.out(_3_out));
  Button _0 (.out(_0_out));
  Button button (.out(button_out));
  Button button_2 (.out(button_2_out));
  Button azzera (.out(azzera_out));
  Button annulla (.out(annulla_out));
  Hex_Digit_Display hex_digit_display_1 (.value(m_input_memory_1_x_2_saved));  // open: dp
  DotMatrix #(.matrixcols(3), .matrixrows(3)) dotmatrix_1 (
    .col0(m_op_code_displayer_1_out_2), .col1(m_op_code_displayer_1_out_3), .col2(m_op_code_displayer_1_out_4));
  m_op_code_displayer m_op_code_displayer_1 (
    .op_code(op_code), .out_2(m_op_code_displayer_1_out_2), .out_3(m_op_code_displayer_1_out_3),
    .out_4(m_op_code_displayer_1_out_4));
  // m_ui m_ui_1: pin names not known; wires that end beside it: _9_out, _8_out, _7_out, _6_out, _5_out, _4_out, _3_out, _2_out, _1_out, _0_out, reset_out, azzera_out, annulla_out, ok_out, button_out, button_2_out, m_ui_1_p17, op_code, m_ui_1_p19, select, m_ui_1_p21, m_ui_1_p22, m_ui_1_p23, m_ui_1_p24, m_ui_1_p25, m_ui_1_p26, m_ui_1_p27, m_ui_1_p28, m_ui_1_p29, m_ui_1_p30, m_ui_1_p31
  Button load (.out(m_ui_1_p19));
  Button save (.out(m_ui_1_p17));
  Button canc (.out(m_ui_1_p21));
  Hex_Digit_Display hex_digit_display_2 (.value(m_input_memory_1_q_saved));  // open: dp
  Hex_Digit_Display hex_digit_display_3 (.value(m_input_memory_1_x_saved));  // open: dp
  Button operation (.out(m_ui_1_p23));
  m_selection_displayer m_selection_displayer_1 (
    .select(select), .out_2(m_selection_displayer_1_out_2), .out_3(m_selection_displayer_1_out_3),
    .out_4(m_selection_displayer_1_out_4));
  LED led_1 (.in(m_selection_displayer_1_out_3));
  LED led_2 (.in(m_selection_displayer_1_out_2));
  Hex_Digit_Display hex_digit_display_4 (.value(m_input_memory_1_x));  // open: dp
  Hex_Digit_Display hex_digit_display_5 (.value(m_input_memory_1_x_2));  // open: dp
  m_input_memory m_input_memory_1 (
    .data(m_ui_1_p22), .click(m_ui_1_p24), .reset(m_ui_1_p25), .azzera(m_ui_1_p26), .back(m_ui_1_p27),
    .ok(m_ui_1_p28), .save(m_ui_1_p29), .load(m_ui_1_p30), .cancella(m_ui_1_p31), .select(select),
    .x_2(m_input_memory_1_x_2), .x(m_input_memory_1_x), .q(m_input_memory_1_q),
    .x_2_saved(m_input_memory_1_x_2_saved), .x_saved(m_input_memory_1_x_saved),
    .q_saved(m_input_memory_1_q_saved));
  Clock clock_1 (.out(clock_1_out));
  LED led_3 (.in(m_selection_displayer_1_out_4));
  Hex_Digit_Display hex_digit_display_6 (.value(m_input_memory_1_q));  // open: dp
  m_calcolatore m_calcolatore_1 (
    .c_x_2(m_input_memory_1_x_2), .c_x(m_input_memory_1_x), .q(m_input_memory_1_q), .clock(clock_1_out),
    .reset(m_ui_1_p25), .y(m_calcolatore_1_y), .of(m_calcolatore_1_of), .x(m_calcolatore_1_x));
  DotMatrix #(.matrixcols(32), .matrixrows(32)) dotmatrix_2 (
    .col0(m_drawer_1_p8), .col1(m_drawer_1_p9), .col2(m_drawer_1_p10), .col3(m_drawer_1_p11),
    .col4(m_drawer_1_p12), .col5(m_drawer_1_p13), .col6(m_drawer_1_p14), .col7(m_drawer_1_p15),
    .col8(m_drawer_1_p16), .col9(m_drawer_1_p17), .col10(m_drawer_1_p18), .col11(m_drawer_1_p19),
    .col12(m_drawer_1_p20), .col13(m_drawer_1_p21), .col14(m_drawer_1_p22), .col15(m_drawer_1_p23),
    .col16(m_drawer_1_p24), .col17(m_drawer_1_p25), .col18(m_drawer_1_p26), .col19(m_drawer_1_p27),
    .col20(m_drawer_1_p28), .col21(m_drawer_1_p29), .col22(m_drawer_1_p30), .col23(m_drawer_1_p31),
    .col24(m_drawer_1_p32), .col25(m_drawer_1_p33), .col26(m_drawer_1_p34), .col27(m_drawer_1_p35),
    .col28(m_drawer_1_p36), .col29(m_drawer_1_p37), .col30(m_drawer_1_p38), .col31(m_drawer_1_p39));
  // m_drawer m_drawer_1: pin names not known; wires that end beside it: m_calcolatore_1_x, m_calcolatore_1_y, m_calcolatore_1_of, m_ui_1_p25, m_ui_1_p29, m_ui_1_p31, op_code, m_drawer_1_p8, m_drawer_1_p9, m_drawer_1_p10, m_drawer_1_p11, m_drawer_1_p12, m_drawer_1_p13, m_drawer_1_p14, m_drawer_1_p15, m_drawer_1_p16, m_drawer_1_p17, m_drawer_1_p18, m_drawer_1_p19, m_drawer_1_p20, m_drawer_1_p21, m_drawer_1_p22, m_drawer_1_p23, m_drawer_1_p24, m_drawer_1_p25, m_drawer_1_p26, m_drawer_1_p27, m_drawer_1_p28, m_drawer_1_p29, m_drawer_1_p30, m_drawer_1_p31, m_drawer_1_p32, m_drawer_1_p33, m_drawer_1_p34, m_drawer_1_p35, m_drawer_1_p36, m_drawer_1_p37, m_drawer_1_p38, m_drawer_1_p39

  // Notes on the sheet:
  //   x^2
  //   OP
  //   SALVATO
  //   q
  //   x
  //   ATTUALE
  //   x
  //   x^2
  //   q
endmodule
